// Logisim project main.circ as structural Verilog: 2 circuits, main circuit main
module main (
);

  wire A_out, cdm_8_mark5_1_p2, cdm_8_mark5_1_p3, clock_1_out, D_out, not_1_out, or_1_out, R_out, S_out,
       W_out;
  wire [1:0] multiplexer_1_out, or_2_out;
  wire [3:0] apple_X, apple_Y;
  wire [7:0] cdm_8_mark5_1_p4, cdm_8_mark5_1_p5;
  wire [15:0] main_1_row_1, main_1_row_2, main_1_row_3, main_1_row_4, main_1_row_5, main_1_row_6,
       main_1_row_7, main_1_row_8, main_1_row_9, main_1_row_10, main_1_row_11, main_1_row_12, main_1_row_13,
       main_1_row_14, main_1_row_15, main_1_row_16;

  Multiplexer #(.width(2), .enable("false")) multiplexer_1 (
    .in0(2'b00), .in1(or_2_out), .out(multiplexer_1_out), .sel(or_1_out));
  DotMatrix #(.inputtype("row"), .matrixcols(16), .matrixrows(16)) dotmatrix_1 (
    .row0(main_1_row_1), .row1(main_1_row_2), .row2(main_1_row_3), .row3(main_1_row_4), .row4(main_1_row_5),
    .row5(main_1_row_6), .row6(main_1_row_7), .row7(main_1_row_8), .row8(main_1_row_9), .row9(main_1_row_10),
    .row10(main_1_row_11), .row11(main_1_row_12), .row12(main_1_row_13), .row13(main_1_row_14),
    .row14(main_1_row_15), .row15(main_1_row_16));
  graphics_card_main main_1 (
    .row_1(main_1_row_1), .row_2(main_1_row_2), .row_3(main_1_row_3), .row_4(main_1_row_4),
    .row_5(main_1_row_5), .row_6(main_1_row_6), .row_7(main_1_row_7), .row_8(main_1_row_8),
    .row_9(main_1_row_9), .row_10(main_1_row_10), .row_11(main_1_row_11), .row_12(main_1_row_12),
    .row_13(main_1_row_13), .row_14(main_1_row_14), .row_15(main_1_row_15), .row_16(main_1_row_16),
    .apple_X(apple_X), .apple_Y(apple_Y));
  or or_1 (or_1_out, W_out, A_out, S_out, D_out);
  or or_2 (or_2_out[0], A_out, S_out);
  or or_3 (or_2_out[1], S_out, D_out);
  Button W (.out(W_out));
  Button A (.out(A_out));
  Button S (.out(S_out));
  Button R (.out(R_out));
  Button D (.out(D_out));
  generator_apple generator_apple_1 (.in_1(R_out), .apple_Y(apple_X));  // open: apple_X
  Clock clock_1 (.out(clock_1_out));
  generator_apple generator_apple_2 (.in_1(R_out), .apple_X(apple_Y));  // open: apple_Y
  // CdM_8_mark5 cdm_8_mark5_1: pin names not known; wires that end beside it: clock_1_out, cdm_8_mark5_1_p2, cdm_8_mark5_1_p3, cdm_8_mark5_1_p4, cdm_8_mark5_1_p5, cdm_8_mark5_1_p5
  RAM ram_1 (
    .addr(cdm_8_mark5_1_p4), .data(cdm_8_mark5_1_p5), .sel(cdm_8_mark5_1_p2), .clk(clock_1_out),
    .ld(not_1_out), .clr(cdm_8_mark5_1_p3));
  not not_1 (not_1_out, cdm_8_mark5_1_p3);
endmodule

module generator_apple (
  input  in_1,
  output [3:0] apple_X,
  output [3:0] apple_Y
);

  wire _00_checker, and_1_out, comparator_1_eq, comparator_2_eq;
  wire [3:0] random_1_out, random_2_out, transistor_1_out, transistor_2_out;

  Random #(.width(4)) random_1 (.clk(in_1), .out(random_1_out));  // open: next, clr
  Random #(.width(4)) random_2 (.clk(in_1), .out(random_2_out));  // open: next, clr
  Transistor #(.width(4)) transistor_1 (.in(random_2_out), .out(transistor_1_out), .gate(_00_checker));
  Transistor #(.width(4)) transistor_2 (.in(random_1_out), .out(transistor_2_out), .gate(_00_checker));
  Comparator #(.width(4)) comparator_1 (.a(random_1_out), .b(random_2_out), .eq(comparator_1_eq));  // open: gt, lt
  Comparator #(.width(4)) comparator_2 (.a(random_2_out), .b(4'b0000), .eq(comparator_2_eq));  // open: gt, lt
  not not_1 (_00_checker, and_1_out);
  and and_1 (and_1_out, comparator_1_eq, comparator_2_eq);
  Transistor #(.width(4)) transistor_3 (.in(random_1_out), .out(apple_X), .gate(and_1_out));
  Adder #(.width(4)) adder_1 (.a(transistor_1_out), .b(4'b0001), .out(apple_Y));  // open: cin, cout
  Adder #(.width(4)) adder_2 (.a(transistor_2_out), .b(4'b0001), .out(apple_X));  // open: cin, cout
  Transistor #(.width(4)) transistor_4 (.in(random_2_out), .out(apple_Y), .gate(and_1_out));
endmodule
